# Fritzing sketch smartwatch (saved by Fritzing 0.9.3b)
perfboards: 1

parts:
  Part1 = Itsy Bitsy 32u4 3V @ 8MHz [part_number="Adafruit 3675"]
  Part2 = Bluetooth HC-05 Macho
  Part3 = OLED Monochrome 128x64 1.3 inch [part_number=938]
  Part5 = Triple Axis Accelerometer Breakout - ADXL345
  S1 = Pushbutton [package="[THT]"]
  S2 = Pushbutton [package="[THT]"]
  POT1 = Breadboard Trimpot
  Part6 = Adafruit Pro Trinket LiIon/LiPoly Backpack [part_number="Adafruit #2124"]
  U1 = LIPO-110mAh [package=lipo-110]  # not connected
  S3 = Toggle Switch [package=THT]
  U2 = Vibration Motor- ROB-08449 [package=vibe-motor-10mm]
  R1 = Resistor [tolerance=±5% resistance=220 package="0805 [SMD]"]
  S4 = Pushbutton [package="[THT]"]

nets:
  N1: Part1.D4, Part3.RESET
  N2: Part1.D6, R1.Pin_0
  N3: Part1.VBAT, Part6.VBAT
  GND: Part1.GND, Part2.GND, Part3.GND, Part6.GND, S4.Pin_1
  N4: Part1.VBUS, Part6.VBUS
  N5: Part1.D11, Part2.TXD
  N6: Part1.D10, Part2.RXD
  N7: Part1.D9, Part5.CS
  N8: Part1.D7, S1.Pin_3, S1.Pin_4
  N9: Part1.D5_OUT, S2.Pin_3, S2.Pin_4
  N10: Part1.SCL, Part3.SCLK_SCK
  N11: Part1.SDA, Part3.MOSI_SDA
  N12: Part1.MISO, Part5.SDO
  N13: Part1.MOSI, Part5.SDA
  N14: Part1.SCK, Part5.SCL
  N15: Part1.A0, POT1.PIN2
  +3V3: Part1.+3V3, Part2.VCC
  N16: Part1.RST, S4.Pin_3
  VIN: Part3.VIN, Part5.VCC
  N17: Part5.GND, POT1.PIN3
  N18: S1.Pin_1, S1.Pin_2, S2.Pin_1, S2.Pin_2
  N19: Part6.SW2, S3.COM
  N20: Part6.SW1, S3.L1
  N21: U2.-, R1.Pin_1

custom parts:
  Itsy Bitsy 32u4 3V @ 8MHz: What's smaller than a Feather but larger than a Trinket? It's an Itsy Bitsy! Small, powerful, Arduino-compatible - this microcontroller board is perfect when you want something very compact, but still with a bunch of pins. Itsy Bitsy is only 1.4" long by 0.7" wide, but has 6 power pins, 6 analog & digital pins and 17 digital pins. It packs much of the same capability as an Arduino UNO or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
  OLED Monochrome 128x64 1.3 inch: These displays are small, only about 1.3" diagonal, but very readable due to the high contrast of an OLED display. This display is made of 128x64 individual white OLED pixels, each one is turned on or off by the controller chip. Because the display makes its own light, no backlight is required. This reduces the power required to run the OLED and is why the display has such high contrast; we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
  Adafruit Pro Trinket LiIon/LiPoly Backpack: If you have a Pro Trinket you probably know it's the perfect little size for a portable project. This LiPoly backpack makes it really easy to do! Instead of wiring 2 or 3 boards together to make a charging system, this little PCB sits on top of the Pro Trinket and allows a LiPoly/LiIon battery to plug in. When the Pro Trinket USB port is powered, the battery is recharged automatically. Unplug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
